# Fritzing sketch wiring-diagram (saved by Fritzing 0.8.3b)

parts:
  RaspberryPi1 = Raspberry Pi Model B
  J1 = Piezo Speaker

nets:
  N1: RaspberryPi1.3V3, J1.pin1

custom parts:
  Raspberry Pi Model B: Raspberry Pi (Model B)
